// Logisim project 17_NAND as UNIVERSAL GATE (1).circ as structural Verilog: 1 circuit, main circuit main
module main (
  input  in_1,
  input  in_2,
  input  in_3,
  input  in_4,
  input  in_5,
  input  in_6,
  input  in_7,
  output out_8,
  output out_9,
  output out_10,
  output out_11
);

  wire nand_1_out, nand_2_out, nand_3_out, nand_4_out, nand_6_out, nand_7_out, nand_9_out;

  not nand_1 (nand_1_out, in_7);  // NAND_Gate
  not nand_2 (nand_2_out, in_1);  // NAND_Gate
  not nand_3 (nand_3_out, in_4);  // NAND_Gate
  not nand_4 (nand_4_out, in_6);  // NAND_Gate
  nand nand_5 (out_9, nand_2_out, nand_3_out);
  nand nand_6 (nand_6_out, nand_4_out, in_7);
  nand nand_7 (nand_7_out, in_6, nand_1_out);
  nand nand_8 (out_11, nand_6_out, nand_7_out);
  nand nand_9 (nand_9_out, in_2, in_3);
  not nand_10 (out_8, nand_9_out);  // NAND_Gate
  not nand_11 (out_10, in_5);  // NAND_Gate

  // Notes on the sheet:
  //   OR gate using NAND
  //   EX-OR using NAND gate
  //   AND gate using NAND
  //   NOT gate using NAND
endmodule
