// Logisim project 17_NOR as UNIVERSAL (1).circ as structural Verilog: 1 circuit, main circuit main
module main (
  input  in_1,
  input  in_2,
  input  in_3,
  input  in_4,
  input  in_5,
  input  in_6,
  input  in_7,
  output out_8,
  output out_9,
  output out_10
);

  wire nor_1_out, nor_3_out, nor_4_out, nor_5_out, nor_6_out, nor_7_out, nor_10_out, nor_11_out;

  nor nor_1 (nor_1_out, in_2, in_3);
  // NOR_Gate nor_2 has open pins: in0=nor_1_out, in1=nor_1_out, out=open
  nor nor_3 (nor_3_out, in_5, in_5);
  nor nor_4 (nor_4_out, in_6, in_6);
  nor nor_5 (nor_5_out, nor_3_out, in_6);
  nor nor_6 (nor_6_out, nor_4_out, in_5);
  nor nor_7 (nor_7_out, nor_5_out, nor_6_out);
  nor nor_8 (out_9, nor_7_out, nor_7_out);
  not nor_9 (out_10, in_7);  // NOR_Gate
  nor nor_10 (nor_10_out, in_4, in_4);
  nor nor_11 (nor_11_out, in_1, in_1);
  nor nor_12 (out_8, nor_11_out, nor_10_out);

  // Notes on the sheet:
  //   OR using NOR
  //   EX-OR using NOR GATE
  //   NOT using NOR
  //   AND using NOR
endmodule
