// Logisim project 3bit asynchronous.circ as structural Verilog: 1 circuit, main circuit main
module main (
  input  in_1,
  output out_2,
  output out_3,
  output out_4
);

  wire clock_1_out, t_ff_1_qn, t_ff_2_qn;

  Clock clock_1 (.out(clock_1_out));
  T_Flip_Flop t_ff_1 (.clk(clock_1_out), .T(in_1), .Q(out_2), .Qn(t_ff_1_qn));  // open: preset, reset, en
  T_Flip_Flop t_ff_2 (.clk(t_ff_1_qn), .T(in_1), .Q(out_3), .Qn(t_ff_2_qn));  // open: preset, reset, en
  T_Flip_Flop t_ff_3 (.clk(t_ff_2_qn), .T(in_1), .Q(out_4));  // open: Qn, preset, reset, en
endmodule
