// Logisim project 4-bit bcd adder.circ as structural Verilog: 1 circuit, main circuit main
module main (
  input  [3:0] in_1,
  input  [3:0] in_2,
  output [3:0] out_3,
  output out_4
);

  wire and_1_out, and_2_out;
  wire [3:0] adder_1_out;

  Adder #(.width(4)) adder_1 (.a(in_1), .b(in_2), .out(adder_1_out), .cout(out_4));  // open: cin
  and and_1 (and_1_out, adder_1_out[3], adder_1_out[2]);
  and and_2 (and_2_out, adder_1_out[1], adder_1_out[3]);
  Adder #(.width(4)) adder_2 (.a(adder_1_out), .b({1'b0, {2{out_4}}, 1'b0}), .out(out_3));  // open: cin, cout
  or or_1 (out_4, and_2_out, out_4, and_1_out);

  // Notes on the sheet:
  //   PRACTICAL_5
endmodule
