// Logisim project BCD_to_8-4-2-1_converter_PR4_C.circ as structural Verilog: 1 circuit, main circuit main
module main (
  input  A,
  input  B,
  input  C,
  input  D,
  output F1,
  output F2,
  output F3,
  output F4
);

  wire and_1_out, and_2_out, and_3_out, and_4_out, and_5_out, not_1_out, not_2_out, not_3_out;

  not not_1 (not_1_out, B);
  not not_2 (not_2_out, C);
  not not_3 (not_3_out, D);
  and and_1 (and_1_out, B, C);
  and and_2 (and_2_out, B, D);
  and and_3 (and_3_out, B, not_2_out, not_3_out);
  and and_4 (and_4_out, not_1_out, C);
  and and_5 (and_5_out, not_1_out, D);
  xor xor_1 (F3, C, D);
  or or_1 (F1, A, and_1_out, and_2_out);
  or or_2 (F2, and_3_out, and_4_out, and_5_out);

  assign F4 = D;

  // Notes on the sheet:
  //   PRACTICAL_4C
endmodule
