// Logisim project PR4_D_2421_to_84-2-1_converter.circ as structural Verilog: 1 circuit, main circuit main
module main (
  input  A,
  input  B,
  input  C,
  input  in_4,
  output F1,
  output F2,
  output F3,
  output F4
);

  wire and_1_out, and_2_out, and_3_out, and_4_out, and_5_out, and_6_out, and_7_out, and_8_out, not_1_out,
       not_2_out, not_3_out;

  not not_1 (not_1_out, A);
  not not_2 (not_2_out, C);
  not not_3 (not_3_out, in_4);
  and and_1 (and_1_out, B, C, in_4);
  and and_2 (and_2_out, not_1_out, B);
  and and_3 (and_3_out, not_1_out, C);
  and and_4 (and_4_out, not_1_out, in_4);
  and and_5 (and_5_out, A, not_2_out, not_3_out);
  and and_6 (and_6_out, not_1_out, not_2_out, in_4);
  and and_7 (and_7_out, A, C, in_4);
  and and_8 (and_8_out, not_1_out, C, not_3_out);
  or or_1 (F2, and_1_out, and_2_out, and_3_out, and_4_out);
  or or_2 (F3, and_5_out, and_6_out, and_7_out, and_8_out);

  assign F1 = A;
  assign F4 = in_4;

  // Notes on the sheet:
  //   D
  //   PRACTICAL_4D
endmodule
