// Logisim project PRAC_9.circ as structural Verilog: 1 circuit, main circuit main
module main (
  output Qa,
  output Qb,
  output Qc,
  output Qd
);

  wire and_1_out, clock_1_out;

  and and_1 (and_1_out, Qd, Qa);
  Clock clock_1 (.out(clock_1_out));
  T_Flip_Flop t_ff_1 (.clk(clock_1_out), .T(1'b1), .Q(Qa), .reset(and_1_out));  // open: Qn, preset, en
  T_Flip_Flop t_ff_2 (.clk(Qa), .T(1'b1), .Q(Qb), .reset(and_1_out));  // open: Qn, preset, en
  T_Flip_Flop t_ff_3 (.clk(Qb), .T(1'b1), .Q(Qc), .reset(and_1_out));  // open: Qn, preset, en
  T_Flip_Flop t_ff_4 (.clk(Qc), .T(1'b1), .Q(Qd), .reset(and_1_out));  // open: Qn, preset, en

  // Notes on the sheet:
  //   Practical:9
endmodule
