// Logisim project Practical8 (1).circ as structural Verilog: 1 circuit, main circuit main
module main (
  output out_1,
  output out_2,
  output out_3
);

  wire and_1_out, clock_1_out, not_1_out;

  Clock clock_1 (.out(clock_1_out));
  not not_1 (not_1_out, out_3);
  J_K_Flip_Flop j_k_ff_1 (.J(and_1_out), .clk(clock_1_out), .K(and_1_out), .Q(out_1));  // open: Qn, preset, en, reset
  and and_1 (and_1_out, out_2, out_3);
  J_K_Flip_Flop j_k_ff_2 (.J(out_3), .clk(clock_1_out), .K(out_3), .Q(out_2));  // open: Qn, preset, en, reset
  J_K_Flip_Flop j_k_ff_3 (.J(not_1_out), .clk(clock_1_out), .K(out_3), .Q(out_3));  // open: Qn, preset, en, reset

  // Notes on the sheet:
  //   Practical:8
endmodule
