// Logisim project binary_to_gray_pr_4a.circ as structural Verilog: 1 circuit, main circuit main
module main (
  input  A,
  input  B,
  input  C,
  input  D,
  input  G3,
  input  G2,
  input  G1,
  input  G0,
  output G3_2,
  output G2_2,
  output out_11,
  output out_12,
  output A_2,
  output B_2,
  output C_2,
  output D_2
);

  xor xor_1 (B_2, G3, G2);
  xor xor_2 (G2_2, A, B);
  xor xor_3 (out_11, B, C);
  xor xor_4 (out_12, C, D);
  xor xor_5 (C_2, B_2, G1);
  xor xor_6 (D_2, C_2, G0);

  assign A_2 = G3;
  assign G3_2 = A;

  // Notes on the sheet:
  //   PRACTICAL 4A
  //   G1
  //   G0
endmodule
