// Logisim project pr_6_de (1).circ as structural Verilog: 1 circuit, main circuit main
module main (
  input  D,
  input  [2:0] in_2,
  output out_3
);

  wire not_1_out;

  not not_1 (not_1_out, D);
  Multiplexer #(.select(3)) multiplexer_1 (
    .in0(D), .in1(1'b0), .in2(D), .in3(1'b1), .in4(1'b0), .in5(1'b0), .in6(not_1_out), .in7(1'b1),
    .out(out_3), .sel(in_2));  // open: en

  // Notes on the sheet:
  //   PRACTICAL_6
endmodule
