// Logisim project square input number PR4_B (1).circ as structural Verilog: 1 circuit, main circuit main
module main (
  input  x,
  input  y,
  input  z,
  output F1,
  output out_5,
  output out_6,
  output out_7,
  output F6,
  output F5
);

  wire and_2_out, and_3_out, not_1_out, not_2_out, not_3_out, xor_1_out;

  not not_1 (not_1_out, x);
  not not_2 (not_2_out, y);
  not not_3 (not_3_out, z);
  and and_1 (F1, x, y);
  and and_2 (and_2_out, x, not_2_out);
  and and_3 (and_3_out, x, y, y);
  xor xor_1 (xor_1_out, x, y);
  and and_4 (out_7, not_3_out, y);
  or or_1 (out_5, and_2_out, and_3_out);
  and and_5 (out_6, xor_1_out, z);

  assign F5 = 1'b0;
  assign F6 = z;

  // Notes on the sheet:
  //   F4
  //   F2
  //   F3
  //   PRACTICAL_4B
endmodule
